// Logisim project aoc786201-lab04.circ as structural Verilog: 2 circuits, main circuit SC
module SC (
  input  A,
  input  B,
  input  Te,
  output S,
  output Ts
);

  wire and_1_out, and_2_out, and_3_out, xor_1_out;

  and and_1 (and_1_out, A, B);
  and and_2 (and_2_out, A, Te);
  and and_3 (and_3_out, B, Te);
  xor xor_1 (xor_1_out, A, B);
  xor xor_2 (S, xor_1_out, Te);
  or or_1 (Ts, and_1_out, and_2_out, and_3_out);
endmodule

module Somador_subtrator (
  input  SUB,
  input  [3:0] B,
  input  [3:0] A
);

  wire SC0_ts, SC1_ts, SC2_ts, xor_1_out, xor_2_out, xor_3_out, xor_4_out;
  wire [3:0] SC0_s;

  xor xor_1 (xor_1_out, B[0], SUB);
  SC SC0 (.A(A[0]), .B(xor_1_out), .Te(SUB), .S(SC0_s[0]), .Ts(SC0_ts));
  xor xor_2 (xor_2_out, B[1], SUB);
  SC SC1 (.A(A[1]), .B(xor_2_out), .Te(SC0_ts), .S(SC0_s[1]), .Ts(SC1_ts));
  xor xor_3 (xor_3_out, B[2], SUB);
  SC SC2 (.A(A[2]), .B(xor_3_out), .Te(SC1_ts), .S(SC0_s[2]), .Ts(SC2_ts));
  xor xor_4 (xor_4_out, B[3], SUB);
  SC SC3 (.A(A[3]), .B(xor_4_out), .Te(SC2_ts), .S(SC0_s[3]));  // open: Ts
endmodule
